# Fritzing sketch esquema leds (saved by Fritzing 0.9.1b)
breadboards: 1

parts:
  Parte2 = Arduino Mega 2560 (Rev3)
  Parte3 = Arduino Xbee Libellium Shield
  R1 = Resistor [tolerance=±5% resistance=220 package=THT]
  LED1 = LED - 5mm [color="Green (565nm)" package="5 mm [THT]"]
  LED3 = LED - 5mm [color="Orange (612nm)" package="5 mm [THT]"]
  LED4 = LED - 5mm [color="Red (635nm)" package="5 mm [THT]"]
  LED5 = LED - 5mm [color="Blue (470nm)" package="5 mm [THT]"]
  LED6 = LED - 5mm [color="White (8000K)" package="5 mm [THT]"]
  R2 = Resistor [tolerance=±5% resistance=220 package=THT]
  R3 = Resistor [tolerance=±5% resistance=220 package=THT]
  R4 = Resistor [tolerance=±5% resistance=220 package=THT]
  R5 = Resistor [tolerance=±5% resistance=220 package=THT]
  U1 = XBee

nets:
  N1: Parte2.D12_PWM, LED4.cathode
  N2: Parte2.D11_PWM, LED5.cathode
  N3: Parte2.D10_PWM, LED3.cathode
  N4: Parte2.D9_PWM, LED6.cathode
  N5: Parte2.D8_PWM, LED1.cathode
  N6: Parte2.GND, R1.Pin_0, R2.Pin_0, R3.Pin_0, R4.Pin_0, R5.Pin_0
  N7: Parte3.I/08, U1.pin20
  N8: Parte3.I/02, U1.pin19
  N9: Parte3.I/03, U1.pin18
  N10: Parte3.I/06, U1.pin17
  N11: Parte3.I/05, U1.pin16
  N12: Parte3.15, U1.pin15
  N13: Parte3.14, U1.pin14
  N14: Parte3.13, U1.pin13
  N15: Parte3.I/07, U1.pin12
  N16: Parte3.I/04, U1.pin11
  GND: Parte3.GND, U1.GND
  N17: Parte3.9, U1.pin9
  N18: Parte3.8, U1.pin8
  N19: Parte3.PWM1, U1.pin7
  N20: Parte3.PWM0, U1.pin6
  N21: Parte3.RST, U1.pin5
  N22: Parte3.4, U1.pin4
  N23: Parte3.DIN, U1.pin3
  N24: Parte3.DOUT, U1.pin2
  +3V3: Parte3.+3V3, U1.VCC
  N25: R1.Pin_1, LED1.anode
  N26: LED3.anode, R2.Pin_1
  N27: LED4.anode, R3.Pin_1
  N28: LED5.anode, R4.Pin_1
  N29: LED6.anode, R5.Pin_1
