# Fritzing sketch diseño (saved by Fritzing 0.8.3b)
breadboards: 1

parts:
  Parte1 = Arduino Uno (Rev3)
  Parte3 = Arduino XBee Shield
  K1 = Relay [part_number=FRS1B-S package=THT]
  K2 = Relay [part_number=FRS1B-S package=THT]
  K3 = Relay [part_number=FRS1B-S package=THT]
  K4 = Relay [part_number=FRS1B-S package=THT]

nets:
  5V: Parte1.5V, Parte3.5V
  GND: Parte1.GND, Parte3.GND, K1.COIL2, K2.COIL2, K3.COIL2, K4.COIL2
  N1: Parte1.D0/RX, Parte3.UART_RX
  N2: Parte1.D1/TX, Parte3.UART_TX
  N3: Parte1.D4, K3.COIL1
  N4: Parte1.D5_PWM, K1.COIL1
  N5: Parte1.D6_PWM, K2.COIL1
  N6: Parte1.D7, K4.COIL1
  N7: Parte1.RESET, Parte3.RST
